# Fritzing sketch Sense_arduino (saved by Fritzing 0.9.3b)
breadboards: 1

parts:
  T1 = LM35 Temperature Sensor [package="TO92 [THT]"]
  ad623 = OP27 - Low Noise, Precision Op Amp [part_number=OP27]
  R1 = Resistor [tolerance=±5% resistance=1.8k package="1206 [SMD]"]
  R2 = Trimmer Potentiometer [maximum_resistance=1kΩ package=THT]
  R3 = Resistor [tolerance=±5% resistance=118k package="1206 [SMD]"]
  R4 = Resistor [tolerance=±5% resistance=5.7k package="1206 [SMD]"]  # not connected
  R5 = Resistor [tolerance=±5% resistance=100k package="1206 [SMD]"]
  R6 = Resistor [tolerance=±5% resistance=100k package="1206 [SMD]"]

nets:
  N1: T1.+Vs, ad623.-V, R6.Pin_1
  N2: T1.Vout, ad623.+IN
  N3: T1.GND, ad623.V+, R3.Pin_0, R5.Pin_0
  N4: ad623.TRIM#1, R1.Pin_1
  N5: ad623.-IN, R2.wiper
  N6: ad623.NC, R5.Pin_1, R6.Pin_0
  N7: ad623.TRIM#8, R1.Pin_0
  N8: R2.leg2, R3.Pin_1

notes:
  +5V
  Ground
  AD623
  Output
